# Fritzing sketch ArduinoMega2Cansat (saved by Fritzing 0.9.0b)
breadboards: 1

parts:
  Part1 = Arduino Mega 2560 (Rev3)
  J2 = female pin header, 10 pins [form="♀ (female)"]
  J1 = female pin header, 10 pins [form="♀ (female)"]
  J3 = female pin header, 10 pins [form="♀ (female)"]
  J4 = female pin header, 10 pins [form="♀ (female)"]
  J5 = female pin header, 10 pins [form="♀ (female)"]
  J6 = female pin header, 10 pins [form="♀ (female)"]
  R1 = Resistor [tolerance=±5% resistance=20 package=THT]
  R2 = Resistor [tolerance=±5% resistance=220 package=THT]
  R3 = Resistor [tolerance=±5% resistance=20 package=THT]
  R4 = Resistor [tolerance=±5% resistance=20 package=THT]
  R5 = Resistor [tolerance=±5% resistance=20 package=THT]
  R7 = Resistor [tolerance=±5% resistance=20 package=THT]
  R8 = Resistor [tolerance=±5% resistance=20 package=THT]
  R6 = Resistor [tolerance=±5% resistance=20 package=THT]
  LED1 = LED - 3mm [color="Red (633nm)" package="3 mm [THT]"]
  LED2 = LED - 3mm [color="Red (633nm)" package="3 mm [THT]"]
  LED3 = LED - 3mm [color="Red (633nm)" package="3 mm [THT]"]
  LED4 = LED - 3mm [color="Red (633nm)" package="3 mm [THT]"]
  LED7 = LED - 3mm [color="Red (633nm)" package="3 mm [THT]"]
  LED8 = LED - 3mm [color="Red (633nm)" package="3 mm [THT]"]
  LED5 = LED - 3mm [color="Red (633nm)" package="3 mm [THT]"]
  LED6 = LED - 3mm [color="Red (633nm)" package="3 mm [THT]"]

nets:
  N1: Part1.A8, J2.pin9
  N2: Part1.A9, J1.pin9
  N3: Part1.A10, J2.pin8
  N4: Part1.A11, J1.pin8
  N5: Part1.A0, J2.pin7
  N6: Part1.A1, J1.pin7
  N7: Part1.A2, J2.pin6
  N8: Part1.A3, J1.pin6
  N9: Part1.A4, J2.pin5
  N10: Part1.A5, J1.pin5
  N11: Part1.A6, J2.pin4
  N12: Part1.A7, J1.pin4
  N13: Part1.D21/SCL, LED3.anode
  N14: Part1.D20/SDA, LED4.anode
  N15: Part1.D19/RX1, LED5.anode
  N16: Part1.D18/TX1, LED6.anode
  N17: Part1.D17_PWM/RX2, LED7.anode
  N18: Part1.D16_PWM/TX2, LED8.anode
  N19: Part1.D15/RX3, J5.pin2
  N20: Part1.D14/TX3, J6.pin2
  N21: Part1.D13_PWM, J5.pin3
  N22: Part1.D12_PWM, J6.pin3
  N23: Part1.D11_PWM, J5.pin4
  N24: Part1.D10_PWM, J6.pin4
  N25: Part1.D9_PWM, J5.pin5
  N26: Part1.D8_PWM, J6.pin5
  N27: Part1.GND, R1.Pin_1, R2.Pin_1, R3.Pin_1, R4.Pin_1, R5.Pin_1, R7.Pin_1, R8.Pin_1, R6.Pin_1
  N28: Part1.D0_RX0, J6.pin9
  N29: Part1.D1_TX0, J5.pin9
  N30: Part1.D2_PWM, J6.pin8
  N31: Part1.D3_PWM, J5.pin8
  N32: Part1.D4_PWM, J6.pin7
  N33: Part1.D5_PWM, J5.pin7
  N34: Part1.D6_PWM, J6.pin6
  N35: Part1.D7_PWM, J5.pin6
  N36: Part1.D22, LED2.anode
  N37: Part1.D23, LED1.anode
  N38: Part1.D24, J4.pin9
  N39: Part1.D25, J3.pin9
  N40: Part1.D26, J4.pin8
  N41: Part1.D27, J3.pin8
  N42: Part1.D28, J4.pin7
  N43: Part1.D29, J3.pin7
  N44: Part1.D30, J4.pin6
  N45: Part1.D31, J3.pin6
  N46: Part1.D32, J4.pin5
  N47: Part1.D33, J3.pin5
  N48: Part1.D34, J4.pin4
  N49: Part1.D35, J3.pin4
  N50: Part1.D36, J4.pin3
  N51: Part1.D37, J3.pin3
  N52: Part1.D38, J4.pin2
  N53: Part1.D39, J3.pin2
  N54: Part1.D52, J2.pin2
  N55: Part1.D53, J1.pin2
  N56: R1.Pin_0, LED1.cathode
  N57: R2.Pin_0, LED2.cathode
  N58: R3.Pin_0, LED3.cathode
  N59: R4.Pin_0, LED4.cathode
  N60: R5.Pin_0, LED5.cathode
  N61: R7.Pin_0, LED7.cathode
  N62: R8.Pin_0, LED8.cathode
  N63: R6.Pin_0, LED6.cathode
